# Fritzing sketch 00_prueba (saved by Fritzing 0.9.3b)
circuit board: 5.35792cm x 5.58276cm
breadboards: 1

parts:
  1 = Hex Inverter Schmitt Trigger SN74HC14 [package="DIP (Dual Inline)"]
  SN74LS241N = Hex Inverter Schmitt Trigger SN74HC14 [package="DIP (Dual Inline)"]
  Dynamixel = Basic Servo
  +_- = Basic Servo
  R7 = Resistor [tolerance=±5% resistance=220 package=THT]
  R8 = Resistor [tolerance=±5% resistance=220 package=THT]
  R9 = Resistor [tolerance=±5% resistance=220 package=THT]
  LED3 = RGB LED - (4 legs) [package="5 mm [THT]"]
  Raspberry_Pi_3 = Raspberry Pi 3 [part_number=RPI-3-V1.2]

nets:
  N1: 1.1A, 1.6A
  N2: 1.1Y, 1.2A, Dynamixel.pulse
  N3: 1.5Y, Raspberry_Pi_3.GIPO18
  N4: 1.5A, Raspberry_Pi_3.GIPO14
  N5: 1.6Y, Raspberry_Pi_3.GIPO15
  VCC: 1.VCC, +_-.pulse, Raspberry_Pi_3.5V
  GND: SN74LS241N.GND, R7.Pin_1, Raspberry_Pi_3.GND
  GND_2: Dynamixel.gnd, +_-.gnd, LED3.red_cathode
  N6: R7.Pin_0, LED3.blue_cathode
  N7: R8.Pin_0, LED3.green_cathode
  N8: R8.Pin_1, Raspberry_Pi_3.GIPO16
  N9: R9.Pin_0, LED3.common_anode
  N10: R9.Pin_1, Raspberry_Pi_3.GIPO20
